# Fritzing sketch Untitled Sketch (saved by Fritzing 0.9.3b)

parts:
  Part1 = Arduino Mega 2560 (Rev3)
  DS1 = DS18B20 1-Wire Temperature Sensor [part_number=DS18B20]
  R1 = Resistor [tolerance=±5% resistance=220 package=THT]
  Part2 = Real Time Clock Module - DS1307 RTC Breakout Board

nets:
  N1: Part1.D21/SCL, Part2.SCL
  N2: Part1.D20/SDA, Part2.SDA
  GND: Part1.GND, DS1.GND, Part2.GND
  5V: Part1.5V, DS1.VDD, R1.Pin_0, Part2.5V
  N3: Part1.D2_PWM, DS1.DQ, R1.Pin_1
